// Logisim project ula.circ as structural Verilog: 6 circuits, main circuit main
module main (
  input  [31:0] A,
  input  [4:0] in_2,
  input  [31:0] B,
  output [31:0] S,
  output OverFlow
);

  wire and_1_out, multiplexer_1_out, not_1_out, ula_cel_1_cout, ula_cel_2_cout, ula_cel_3_cout,
       ula_cel_4_cout, ula_cel_5_cout, ula_cel_6_cout, ula_cel_7_cout, ula_cel_8_cout, ula_cel_9_cout,
       ula_cel_10_cout, ula_cel_11_cout, ula_cel_12_cout, ula_cel_13_cout, ula_cel_14_cout, ula_cel_15_cout,
       ula_cel_16_cout, ula_cel_17_cout, ula_cel_18_cout, ula_cel_19_cout, ula_cel_20_cout, ula_cel_21_cout,
       ula_cel_22_cout, ula_cel_23_cout, ula_cel_24_cout, ula_cel_25_cout, ula_cel_26_cout, ula_cel_27_cout,
       ula_cel_28_cout, ula_cel_29_cout, ula_cel_30_cout, ula_cel_31_cout, ula_cel_32_cout;
  wire [7:0] undriven, undriven_2, undriven_3, undriven_4;

  and and_1 (and_1_out, ~in_2[4], ~in_2[3], in_2[2], in_2[1], ~in_2[0]);  // AND_Gate
  not not_1 (not_1_out, 1'b0);
  Multiplexer #(.enable("false")) multiplexer_1 (.in0(1'b0), .in1(not_1_out), .out(multiplexer_1_out), .sel(and_1_out));
  ula_cel ula_cel_1 (
    .Cin(multiplexer_1_out), .a(undriven[0]), .b(B[0]), .Select(in_2), .S(S[0]), .Cout(ula_cel_1_cout));
  ula_cel ula_cel_2 (
    .Cin(ula_cel_29_cout), .a(undriven_2[0]), .b(B[8]), .Select(in_2), .S(S[8]), .Cout(ula_cel_2_cout));
  ula_cel ula_cel_3 (
    .Cin(ula_cel_30_cout), .a(undriven_3[0]), .b(B[16]), .Select(in_2), .S(S[16]), .Cout(ula_cel_3_cout));
  ula_cel ula_cel_4 (
    .Cin(ula_cel_31_cout), .a(undriven_4[0]), .b(B[24]), .Select(in_2), .S(S[24]), .Cout(ula_cel_4_cout));
  ula_cel ula_cel_5 (.Cin(ula_cel_1_cout), .a(undriven[1]), .b(B[1]), .Select(in_2), .S(S[1]), .Cout(ula_cel_5_cout));
  ula_cel ula_cel_6 (.Cin(ula_cel_2_cout), .a(undriven_2[1]), .b(B[9]), .Select(in_2), .S(S[9]), .Cout(ula_cel_6_cout));
  ula_cel ula_cel_7 (
    .Cin(ula_cel_3_cout), .a(undriven_3[1]), .b(B[17]), .Select(in_2), .S(S[17]), .Cout(ula_cel_7_cout));
  ula_cel ula_cel_8 (
    .Cin(ula_cel_4_cout), .a(undriven_4[1]), .b(B[25]), .Select(in_2), .S(S[25]), .Cout(ula_cel_8_cout));
  ula_cel ula_cel_9 (.Cin(ula_cel_5_cout), .a(undriven[2]), .b(B[2]), .Select(in_2), .S(S[2]), .Cout(ula_cel_9_cout));
  ula_cel ula_cel_10 (
    .Cin(ula_cel_6_cout), .a(undriven_2[2]), .b(B[10]), .Select(in_2), .S(S[10]), .Cout(ula_cel_10_cout));
  ula_cel ula_cel_11 (
    .Cin(ula_cel_7_cout), .a(undriven_3[2]), .b(B[18]), .Select(in_2), .S(S[18]), .Cout(ula_cel_11_cout));
  ula_cel ula_cel_12 (
    .Cin(ula_cel_8_cout), .a(undriven_4[2]), .b(B[26]), .Select(in_2), .S(S[26]), .Cout(ula_cel_12_cout));
  ula_cel ula_cel_13 (.Cin(ula_cel_9_cout), .a(undriven[3]), .b(B[3]), .Select(in_2), .S(S[3]), .Cout(ula_cel_13_cout));
  ula_cel ula_cel_14 (
    .Cin(ula_cel_10_cout), .a(undriven_2[3]), .b(B[11]), .Select(in_2), .S(S[11]), .Cout(ula_cel_14_cout));
  ula_cel ula_cel_15 (
    .Cin(ula_cel_11_cout), .a(undriven_3[3]), .b(B[19]), .Select(in_2), .S(S[19]), .Cout(ula_cel_15_cout));
  ula_cel ula_cel_16 (
    .Cin(ula_cel_12_cout), .a(undriven_4[3]), .b(B[27]), .Select(in_2), .S(S[27]), .Cout(ula_cel_16_cout));
  ula_cel ula_cel_17 (
    .Cin(ula_cel_13_cout), .a(undriven[4]), .b(B[4]), .Select(in_2), .S(S[4]), .Cout(ula_cel_17_cout));
  ula_cel ula_cel_18 (
    .Cin(ula_cel_14_cout), .a(undriven_2[4]), .b(B[12]), .Select(in_2), .S(S[12]), .Cout(ula_cel_18_cout));
  ula_cel ula_cel_19 (
    .Cin(ula_cel_15_cout), .a(undriven_3[4]), .b(B[20]), .Select(in_2), .S(S[20]), .Cout(ula_cel_19_cout));
  ula_cel ula_cel_20 (
    .Cin(ula_cel_16_cout), .a(undriven_4[4]), .b(B[28]), .Select(in_2), .S(S[28]), .Cout(ula_cel_20_cout));
  ula_cel ula_cel_21 (
    .Cin(ula_cel_17_cout), .a(undriven[5]), .b(B[5]), .Select(in_2), .S(S[5]), .Cout(ula_cel_21_cout));
  ula_cel ula_cel_22 (
    .Cin(ula_cel_18_cout), .a(undriven_2[5]), .b(B[13]), .Select(in_2), .S(S[13]), .Cout(ula_cel_22_cout));
  ula_cel ula_cel_23 (
    .Cin(ula_cel_19_cout), .a(undriven_3[5]), .b(B[21]), .Select(in_2), .S(S[21]), .Cout(ula_cel_23_cout));
  ula_cel ula_cel_24 (
    .Cin(ula_cel_20_cout), .a(undriven_4[5]), .b(B[29]), .Select(in_2), .S(S[29]), .Cout(ula_cel_24_cout));
  ula_cel ula_cel_25 (
    .Cin(ula_cel_21_cout), .a(undriven[6]), .b(B[6]), .Select(in_2), .S(S[6]), .Cout(ula_cel_25_cout));
  ula_cel ula_cel_26 (
    .Cin(ula_cel_22_cout), .a(undriven_2[6]), .b(B[14]), .Select(in_2), .S(S[14]), .Cout(ula_cel_26_cout));
  ula_cel ula_cel_27 (
    .Cin(ula_cel_23_cout), .a(undriven_3[6]), .b(B[22]), .Select(in_2), .S(S[22]), .Cout(ula_cel_27_cout));
  ula_cel ula_cel_28 (
    .Cin(ula_cel_24_cout), .a(undriven_4[6]), .b(B[30]), .Select(in_2), .S(S[30]), .Cout(ula_cel_28_cout));
  ula_cel ula_cel_29 (
    .Cin(ula_cel_25_cout), .a(undriven[7]), .b(B[7]), .Select(in_2), .S(S[7]), .Cout(ula_cel_29_cout));
  ula_cel ula_cel_30 (
    .Cin(ula_cel_26_cout), .a(undriven_2[7]), .b(B[15]), .Select(in_2), .S(S[15]), .Cout(ula_cel_30_cout));
  ula_cel ula_cel_31 (
    .Cin(ula_cel_27_cout), .a(undriven_3[7]), .b(B[23]), .Select(in_2), .S(S[23]), .Cout(ula_cel_31_cout));
  ula_cel ula_cel_32 (
    .Cin(ula_cel_28_cout), .a(undriven_4[7]), .b(B[31]), .Select(in_2), .S(S[31]), .Cout(ula_cel_32_cout));
  overflow overflow_1 (
    .OpeCod(in_2), .Cin(ula_cel_32_cout), .S(S[31]), .b(B[31]), .a(undriven_4[7]), .OverFlow(OverFlow));

  // Notes on the sheet:
  //   00000 - And
  //   00001 - Or
  //   00010 - XOR
  //   00011 - NAND
  //   00100 - Soma naturais
  //   00101 - Soma inteiros
endmodule

module ula_cel (
  input  a,
  input  b,
  input  Cin,
  input  [4:0] Select,
  output S,
  output Cout
);

  wire and_1_out, full_adder_1_s, nand_1_out, or_1_out, xor_1_out;

  and and_1 (and_1_out, a, b);
  or or_1 (or_1_out, a, b);
  xor xor_1 (xor_1_out, a, b);
  nand nand_1 (nand_1_out, a, b);
  full_adder full_adder_1 (.in_3(Select), .Cin(Cin), .a(a), .b(b), .s(full_adder_1_s), .Cout(Cout));
  Multiplexer #(.select(5), .enable("false")) multiplexer_1 (
    .in0(and_1_out), .in1(or_1_out), .in2(xor_1_out), .in3(nand_1_out), .in4(full_adder_1_s),
    .in5(full_adder_1_s), .in6(full_adder_1_s), .out(S), .sel(Select));  // open: in7, in8, in9, in10, in11, in12, in13, in14, in15, in16, in17, in18, in19, in20, in21, in22, in23, in24, in25, in26, in27, in28, in29, in30, in31

  // Notes on the sheet:
  //   00000 - And
  //   00001 - Or
  //   00010 - XOR
  //   00011 - NAND
  //   00100 - Soma naturais
  //   00101 - Soma inteiros
  //   00110 - Subtração
endmodule

module full_adder (
  input  a,
  input  b,
  input  [4:0] in_3,
  input  Cin,
  output Cout,
  output s
);

  wire and_1_out, and_2_out, and_3_out, and_4_out, and_5_out, multiplexer_1_out, not_1_out, xor_1_out;

  and and_1 (and_1_out, ~in_3[0], in_3[1], in_3[2], ~in_3[3], ~in_3[4]);  // AND_Gate
  not not_1 (not_1_out, b);
  Multiplexer #(.enable("false")) multiplexer_1 (.in0(b), .in1(not_1_out), .out(multiplexer_1_out), .sel(and_1_out));
  xor xor_1 (xor_1_out, a, multiplexer_1_out);
  xor xor_2 (s, xor_1_out, Cin);
  and and_2 (and_2_out, ~a, multiplexer_1_out, Cin);  // AND_Gate
  and and_3 (and_3_out, a, ~multiplexer_1_out, Cin);  // AND_Gate
  and and_4 (and_4_out, a, multiplexer_1_out, ~Cin);  // AND_Gate
  and and_5 (and_5_out, a, multiplexer_1_out, Cin);
  or or_1 (Cout, and_2_out, and_3_out, and_4_out, and_5_out);
endmodule

module overflow (
  input  Cin,
  input  S,
  input  b,
  input  a,
  input  [4:0] OpeCod,
  output OverFlow
);

  wire and_1_out, and_2_out, and_3_out, and_4_out, or_1_out, or_2_out;

  and and_1 (and_1_out, OpeCod[0], ~OpeCod[1], OpeCod[2], ~OpeCod[3], ~OpeCod[4]);  // AND_Gate
  and and_2 (and_2_out, ~OpeCod[0], OpeCod[1], OpeCod[2], ~OpeCod[3], ~OpeCod[4]);  // AND_Gate
  and and_3 (and_3_out, ~S, b, a);  // AND_Gate
  and and_4 (and_4_out, S, ~b, ~a);  // AND_Gate
  or or_1 (or_1_out, and_1_out, and_2_out);
  or or_2 (or_2_out, and_3_out, and_4_out);
  Multiplexer #(.enable("false")) multiplexer_1 (.in0(Cin), .in1(or_2_out), .out(OverFlow), .sel(or_1_out));

  // Notes on the sheet:
  //   00100 - Soma naturais
  //   00101 - Soma inteiros
endmodule

module deslocador (
  input  [31:0] in_1,
  input  [4:0] OpeCode,
  input  [4:0] move,
  output [31:0] out_4
);

  wire and_2_out, and_3_out, and_4_out, and_5_out, multiplexer_1_out, multiplexer_2_out, multiplexer_3_out,
       multiplexer_4_out, multiplexer_5_out, multiplexer_6_out, multiplexer_7_out, multiplexer_8_out,
       multiplexer_9_out, multiplexer_10_out, multiplexer_11_out, multiplexer_12_out, multiplexer_13_out,
       multiplexer_14_out, multiplexer_15_out, multiplexer_16_out, multiplexer_17_out, multiplexer_18_out,
       multiplexer_19_out, multiplexer_20_out, multiplexer_21_out, multiplexer_22_out, multiplexer_23_out,
       multiplexer_24_out, multiplexer_25_out, multiplexer_26_out, multiplexer_27_out, multiplexer_28_out,
       multiplexer_29_out, multiplexer_30_out, multiplexer_31_out, multiplexer_32_out, multiplexer_33_out,
       multiplexer_34_out, multiplexer_35_out, multiplexer_36_out, multiplexer_37_out, multiplexer_38_out,
       multiplexer_39_out, multiplexer_40_out, multiplexer_41_out, multiplexer_42_out, multiplexer_43_out,
       multiplexer_44_out, multiplexer_45_out, multiplexer_46_out, multiplexer_47_out, multiplexer_48_out,
       multiplexer_49_out, multiplexer_50_out, multiplexer_51_out, multiplexer_52_out, multiplexer_53_out,
       multiplexer_54_out, multiplexer_55_out, multiplexer_56_out, multiplexer_57_out, multiplexer_58_out,
       multiplexer_59_out, multiplexer_60_out, multiplexer_61_out, multiplexer_62_out, multiplexer_63_out,
       multiplexer_64_out, multiplexer_65_out, multiplexer_66_out, multiplexer_67_out, multiplexer_68_out,
       multiplexer_69_out, multiplexer_70_out, multiplexer_71_out, multiplexer_72_out, multiplexer_73_out,
       multiplexer_74_out, multiplexer_75_out, multiplexer_76_out, multiplexer_77_out, multiplexer_78_out,
       multiplexer_79_out, multiplexer_80_out, multiplexer_81_out, multiplexer_82_out, multiplexer_83_out,
       multiplexer_84_out, multiplexer_85_out, multiplexer_86_out, multiplexer_87_out, multiplexer_88_out,
       multiplexer_89_out, multiplexer_90_out, multiplexer_91_out, multiplexer_92_out, multiplexer_93_out,
       multiplexer_94_out, multiplexer_95_out, multiplexer_96_out, multiplexer_97_out, multiplexer_98_out,
       multiplexer_99_out, multiplexer_100_out, multiplexer_101_out, multiplexer_102_out,
       multiplexer_103_out, multiplexer_104_out, multiplexer_105_out, multiplexer_106_out,
       multiplexer_107_out, multiplexer_108_out, multiplexer_109_out, multiplexer_110_out,
       multiplexer_111_out, multiplexer_112_out, multiplexer_113_out, multiplexer_114_out,
       multiplexer_115_out, multiplexer_116_out, multiplexer_117_out, multiplexer_118_out,
       multiplexer_119_out, multiplexer_120_out, multiplexer_121_out, multiplexer_122_out,
       multiplexer_123_out, multiplexer_124_out, multiplexer_125_out, multiplexer_126_out,
       multiplexer_127_out, multiplexer_128_out, multiplexer_129_out, multiplexer_130_out,
       multiplexer_131_out, multiplexer_132_out, multiplexer_133_out, multiplexer_134_out,
       multiplexer_135_out, multiplexer_136_out, multiplexer_137_out, multiplexer_138_out,
       multiplexer_139_out, multiplexer_140_out, multiplexer_141_out, multiplexer_142_out,
       multiplexer_143_out, multiplexer_144_out, multiplexer_145_out, multiplexer_146_out,
       multiplexer_147_out, multiplexer_148_out, multiplexer_149_out, multiplexer_150_out,
       multiplexer_151_out, multiplexer_152_out, multiplexer_153_out, multiplexer_154_out,
       multiplexer_155_out, multiplexer_156_out, multiplexer_157_out, multiplexer_158_out,
       multiplexer_159_out, multiplexer_160_out, not_1_out, not_2_out, not_3_out, not_4_out, not_5_out,
       not_6_out, not_7_out, not_8_out, not_9_out, not_10_out, not_11_out, not_12_out, not_13_out,
       not_14_out, not_15_out;
  wire [1:0] or_1_out;

  Multiplexer #(.enable("false")) multiplexer_1 (.in0(in_1[0]), .in1(in_1[1]), .out(multiplexer_1_out), .sel(move[0]));
  Multiplexer #(.enable("false")) multiplexer_2 (.in0(in_1[1]), .in1(in_1[2]), .out(multiplexer_2_out), .sel(move[0]));
  Multiplexer #(.enable("false")) multiplexer_3 (.in0(in_1[2]), .in1(in_1[3]), .out(multiplexer_3_out), .sel(move[0]));
  Multiplexer #(.enable("false")) multiplexer_4 (.in0(in_1[3]), .in1(in_1[4]), .out(multiplexer_4_out), .sel(move[0]));
  Multiplexer #(.enable("false")) multiplexer_5 (.in0(in_1[4]), .in1(in_1[5]), .out(multiplexer_5_out), .sel(move[0]));
  Multiplexer #(.enable("false")) multiplexer_6 (.in0(in_1[5]), .in1(in_1[6]), .out(multiplexer_6_out), .sel(move[0]));
  Multiplexer #(.enable("false")) multiplexer_7 (.in0(in_1[6]), .in1(in_1[7]), .out(multiplexer_7_out), .sel(move[0]));
  Multiplexer #(.enable("false")) multiplexer_8 (.in0(in_1[7]), .in1(in_1[8]), .out(multiplexer_8_out), .sel(move[0]));
  Multiplexer #(.enable("false")) multiplexer_9 (.in0(in_1[8]), .in1(in_1[9]), .out(multiplexer_9_out), .sel(move[0]));
  Multiplexer #(.enable("false")) multiplexer_10 (
    .in0(in_1[9]), .in1(in_1[10]), .out(multiplexer_10_out), .sel(move[0]));
  Multiplexer #(.enable("false")) multiplexer_11 (
    .in0(in_1[10]), .in1(in_1[11]), .out(multiplexer_11_out), .sel(move[0]));
  Multiplexer #(.enable("false")) multiplexer_12 (
    .in0(in_1[11]), .in1(in_1[12]), .out(multiplexer_12_out), .sel(move[0]));
  Multiplexer #(.enable("false")) multiplexer_13 (
    .in0(in_1[12]), .in1(in_1[13]), .out(multiplexer_13_out), .sel(move[0]));
  Multiplexer #(.enable("false")) multiplexer_14 (
    .in0(in_1[13]), .in1(in_1[14]), .out(multiplexer_14_out), .sel(move[0]));
  Multiplexer #(.enable("false")) multiplexer_15 (
    .in0(in_1[14]), .in1(in_1[15]), .out(multiplexer_15_out), .sel(move[0]));
  Multiplexer #(.enable("false")) multiplexer_16 (
    .in0(in_1[15]), .in1(in_1[16]), .out(multiplexer_16_out), .sel(move[0]));
  Multiplexer #(.enable("false")) multiplexer_17 (
    .in0(in_1[16]), .in1(in_1[17]), .out(multiplexer_17_out), .sel(move[0]));
  Multiplexer #(.enable("false")) multiplexer_18 (
    .in0(in_1[17]), .in1(in_1[18]), .out(multiplexer_18_out), .sel(move[0]));
  Multiplexer #(.enable("false")) multiplexer_19 (
    .in0(in_1[18]), .in1(in_1[19]), .out(multiplexer_19_out), .sel(move[0]));
  Multiplexer #(.enable("false")) multiplexer_20 (
    .in0(in_1[19]), .in1(in_1[20]), .out(multiplexer_20_out), .sel(move[0]));
  Multiplexer #(.enable("false")) multiplexer_21 (
    .in0(in_1[20]), .in1(in_1[21]), .out(multiplexer_21_out), .sel(move[0]));
  Multiplexer #(.enable("false")) multiplexer_22 (
    .in0(in_1[21]), .in1(in_1[22]), .out(multiplexer_22_out), .sel(move[0]));
  Multiplexer #(.enable("false")) multiplexer_23 (
    .in0(in_1[22]), .in1(in_1[23]), .out(multiplexer_23_out), .sel(move[0]));
  Multiplexer #(.enable("false")) multiplexer_24 (
    .in0(in_1[23]), .in1(in_1[24]), .out(multiplexer_24_out), .sel(move[0]));
  Multiplexer #(.enable("false")) multiplexer_25 (
    .in0(in_1[24]), .in1(in_1[25]), .out(multiplexer_25_out), .sel(move[0]));
  Multiplexer #(.enable("false")) multiplexer_26 (
    .in0(in_1[25]), .in1(in_1[26]), .out(multiplexer_26_out), .sel(move[0]));
  Multiplexer #(.enable("false")) multiplexer_27 (
    .in0(in_1[26]), .in1(in_1[27]), .out(multiplexer_27_out), .sel(move[0]));
  Multiplexer #(.enable("false")) multiplexer_28 (
    .in0(in_1[27]), .in1(in_1[28]), .out(multiplexer_28_out), .sel(move[0]));
  Multiplexer #(.enable("false")) multiplexer_29 (
    .in0(in_1[28]), .in1(in_1[29]), .out(multiplexer_29_out), .sel(move[0]));
  Multiplexer #(.enable("false")) multiplexer_30 (
    .in0(in_1[29]), .in1(in_1[30]), .out(multiplexer_30_out), .sel(move[0]));
  Multiplexer #(.enable("false")) multiplexer_31 (
    .in0(in_1[30]), .in1(in_1[31]), .out(multiplexer_31_out), .sel(move[0]));
  Multiplexer #(.enable("false")) multiplexer_32 (
    .in0(in_1[31]), .in1(in_1[0]), .out(multiplexer_32_out), .sel(move[0]));
  Multiplexer #(.enable("false")) multiplexer_33 (
    .in0(multiplexer_1_out), .in1(multiplexer_3_out), .out(multiplexer_33_out), .sel(move[1]));
  Multiplexer #(.enable("false")) multiplexer_34 (
    .in0(multiplexer_2_out), .in1(multiplexer_4_out), .out(multiplexer_34_out), .sel(move[1]));
  Multiplexer #(.enable("false")) multiplexer_35 (
    .in0(multiplexer_3_out), .in1(multiplexer_5_out), .out(multiplexer_35_out), .sel(move[1]));
  Multiplexer #(.enable("false")) multiplexer_36 (
    .in0(multiplexer_4_out), .in1(multiplexer_6_out), .out(multiplexer_36_out), .sel(move[1]));
  Multiplexer #(.enable("false")) multiplexer_37 (
    .in0(multiplexer_5_out), .in1(multiplexer_7_out), .out(multiplexer_37_out), .sel(move[1]));
  Multiplexer #(.enable("false")) multiplexer_38 (
    .in0(multiplexer_6_out), .in1(multiplexer_8_out), .out(multiplexer_38_out), .sel(move[1]));
  Multiplexer #(.enable("false")) multiplexer_39 (
    .in0(multiplexer_7_out), .in1(multiplexer_9_out), .out(multiplexer_39_out), .sel(move[1]));
  Multiplexer #(.enable("false")) multiplexer_40 (
    .in0(multiplexer_8_out), .in1(multiplexer_10_out), .out(multiplexer_40_out), .sel(move[1]));
  Multiplexer #(.enable("false")) multiplexer_41 (
    .in0(multiplexer_9_out), .in1(multiplexer_11_out), .out(multiplexer_41_out), .sel(move[1]));
  Multiplexer #(.enable("false")) multiplexer_42 (
    .in0(multiplexer_10_out), .in1(multiplexer_12_out), .out(multiplexer_42_out), .sel(move[1]));
  Multiplexer #(.enable("false")) multiplexer_43 (
    .in0(multiplexer_11_out), .in1(multiplexer_13_out), .out(multiplexer_43_out), .sel(move[1]));
  Multiplexer #(.enable("false")) multiplexer_44 (
    .in0(multiplexer_12_out), .in1(multiplexer_14_out), .out(multiplexer_44_out), .sel(move[1]));
  Multiplexer #(.enable("false")) multiplexer_45 (
    .in0(multiplexer_13_out), .in1(multiplexer_15_out), .out(multiplexer_45_out), .sel(move[1]));
  Multiplexer #(.enable("false")) multiplexer_46 (
    .in0(multiplexer_14_out), .in1(multiplexer_16_out), .out(multiplexer_46_out), .sel(move[1]));
  Multiplexer #(.enable("false")) multiplexer_47 (
    .in0(multiplexer_15_out), .in1(multiplexer_17_out), .out(multiplexer_47_out), .sel(move[1]));
  Multiplexer #(.enable("false")) multiplexer_48 (
    .in0(multiplexer_16_out), .in1(multiplexer_18_out), .out(multiplexer_48_out), .sel(move[1]));
  Multiplexer #(.enable("false")) multiplexer_49 (
    .in0(multiplexer_17_out), .in1(multiplexer_19_out), .out(multiplexer_49_out), .sel(move[1]));
  Multiplexer #(.enable("false")) multiplexer_50 (
    .in0(multiplexer_18_out), .in1(multiplexer_20_out), .out(multiplexer_50_out), .sel(move[1]));
  Multiplexer #(.enable("false")) multiplexer_51 (
    .in0(multiplexer_19_out), .in1(multiplexer_21_out), .out(multiplexer_51_out), .sel(move[1]));
  Multiplexer #(.enable("false")) multiplexer_52 (
    .in0(multiplexer_20_out), .in1(multiplexer_22_out), .out(multiplexer_52_out), .sel(move[1]));
  Multiplexer #(.enable("false")) multiplexer_53 (
    .in0(multiplexer_21_out), .in1(multiplexer_23_out), .out(multiplexer_53_out), .sel(move[1]));
  Multiplexer #(.enable("false")) multiplexer_54 (
    .in0(multiplexer_22_out), .in1(multiplexer_24_out), .out(multiplexer_54_out), .sel(move[1]));
  Multiplexer #(.enable("false")) multiplexer_55 (
    .in0(multiplexer_23_out), .in1(multiplexer_25_out), .out(multiplexer_55_out), .sel(move[1]));
  Multiplexer #(.enable("false")) multiplexer_56 (
    .in0(multiplexer_24_out), .in1(multiplexer_26_out), .out(multiplexer_56_out), .sel(move[1]));
  Multiplexer #(.enable("false")) multiplexer_57 (
    .in0(multiplexer_25_out), .in1(multiplexer_27_out), .out(multiplexer_57_out), .sel(move[1]));
  Multiplexer #(.enable("false")) multiplexer_58 (
    .in0(multiplexer_26_out), .in1(multiplexer_28_out), .out(multiplexer_58_out), .sel(move[1]));
  Multiplexer #(.enable("false")) multiplexer_59 (
    .in0(multiplexer_27_out), .in1(multiplexer_29_out), .out(multiplexer_59_out), .sel(move[1]));
  Multiplexer #(.enable("false")) multiplexer_60 (
    .in0(multiplexer_28_out), .in1(multiplexer_30_out), .out(multiplexer_60_out), .sel(move[1]));
  Multiplexer #(.enable("false")) multiplexer_61 (
    .in0(multiplexer_29_out), .in1(multiplexer_31_out), .out(multiplexer_61_out), .sel(move[1]));
  Multiplexer #(.enable("false")) multiplexer_62 (
    .in0(multiplexer_30_out), .in1(multiplexer_32_out), .out(multiplexer_62_out), .sel(move[1]));
  Multiplexer #(.enable("false")) multiplexer_63 (
    .in0(multiplexer_31_out), .in1(multiplexer_1_out), .out(multiplexer_63_out), .sel(move[1]));
  Multiplexer #(.enable("false")) multiplexer_64 (
    .in0(multiplexer_32_out), .in1(multiplexer_2_out), .out(multiplexer_64_out), .sel(move[1]));
  not not_1 (not_1_out, OpeCode[4]);
  not not_2 (not_2_out, OpeCode[2]);
  not not_3 (not_3_out, OpeCode[1]);
  not not_4 (not_4_out, OpeCode[4]);
  not not_5 (not_5_out, OpeCode[3]);
  not not_6 (not_6_out, OpeCode[2]);
  not not_7 (not_7_out, OpeCode[4]);
  not not_8 (not_8_out, OpeCode[3]);
  not not_9 (not_9_out, OpeCode[1]);
  not not_10 (not_10_out, OpeCode[4]);
  not not_11 (not_11_out, OpeCode[3]);
  not not_12 (not_12_out, OpeCode[0]);
  not not_13 (not_13_out, OpeCode[4]);
  not not_14 (not_14_out, OpeCode[2]);
  not not_15 (not_15_out, OpeCode[1]);
  and and_1 (or_1_out[1], not_1_out, OpeCode[3], not_2_out, not_3_out);
  and and_2 (and_2_out, not_4_out, not_5_out, not_6_out);
  and and_3 (and_3_out, not_7_out, not_8_out, not_9_out);
  and and_4 (and_4_out, not_10_out, not_11_out, not_12_out);
  and and_5 (and_5_out, not_13_out, not_14_out, not_15_out, OpeCode[0]);
  Multiplexer #(.enable("false")) multiplexer_65 (
    .in0(multiplexer_33_out), .in1(multiplexer_37_out), .out(multiplexer_65_out), .sel(move[2]));
  Multiplexer #(.enable("false")) multiplexer_66 (
    .in0(multiplexer_34_out), .in1(multiplexer_38_out), .out(multiplexer_66_out), .sel(move[2]));
  Multiplexer #(.enable("false")) multiplexer_67 (
    .in0(multiplexer_35_out), .in1(multiplexer_39_out), .out(multiplexer_67_out), .sel(move[2]));
  Multiplexer #(.enable("false")) multiplexer_68 (
    .in0(multiplexer_36_out), .in1(multiplexer_40_out), .out(multiplexer_68_out), .sel(move[2]));
  Multiplexer #(.enable("false")) multiplexer_69 (
    .in0(multiplexer_37_out), .in1(multiplexer_41_out), .out(multiplexer_69_out), .sel(move[2]));
  Multiplexer #(.enable("false")) multiplexer_70 (
    .in0(multiplexer_38_out), .in1(multiplexer_42_out), .out(multiplexer_70_out), .sel(move[2]));
  Multiplexer #(.enable("false")) multiplexer_71 (
    .in0(multiplexer_39_out), .in1(multiplexer_43_out), .out(multiplexer_71_out), .sel(move[2]));
  Multiplexer #(.enable("false")) multiplexer_72 (
    .in0(multiplexer_40_out), .in1(multiplexer_44_out), .out(multiplexer_72_out), .sel(move[2]));
  Multiplexer #(.enable("false")) multiplexer_73 (
    .in0(multiplexer_41_out), .in1(multiplexer_45_out), .out(multiplexer_73_out), .sel(move[2]));
  Multiplexer #(.enable("false")) multiplexer_74 (
    .in0(multiplexer_42_out), .in1(multiplexer_46_out), .out(multiplexer_74_out), .sel(move[2]));
  Multiplexer #(.enable("false")) multiplexer_75 (
    .in0(multiplexer_43_out), .in1(multiplexer_47_out), .out(multiplexer_75_out), .sel(move[2]));
  Multiplexer #(.enable("false")) multiplexer_76 (
    .in0(multiplexer_44_out), .in1(multiplexer_48_out), .out(multiplexer_76_out), .sel(move[2]));
  Multiplexer #(.enable("false")) multiplexer_77 (
    .in0(multiplexer_45_out), .in1(multiplexer_49_out), .out(multiplexer_77_out), .sel(move[2]));
  Multiplexer #(.enable("false")) multiplexer_78 (
    .in0(multiplexer_46_out), .in1(multiplexer_50_out), .out(multiplexer_78_out), .sel(move[2]));
  Multiplexer #(.enable("false")) multiplexer_79 (
    .in0(multiplexer_47_out), .in1(multiplexer_51_out), .out(multiplexer_79_out), .sel(move[2]));
  Multiplexer #(.enable("false")) multiplexer_80 (
    .in0(multiplexer_48_out), .in1(multiplexer_52_out), .out(multiplexer_80_out), .sel(move[2]));
  Multiplexer #(.enable("false")) multiplexer_81 (
    .in0(multiplexer_49_out), .in1(multiplexer_53_out), .out(multiplexer_81_out), .sel(move[2]));
  Multiplexer #(.enable("false")) multiplexer_82 (
    .in0(multiplexer_50_out), .in1(multiplexer_54_out), .out(multiplexer_82_out), .sel(move[2]));
  Multiplexer #(.enable("false")) multiplexer_83 (
    .in0(multiplexer_51_out), .in1(multiplexer_55_out), .out(multiplexer_83_out), .sel(move[2]));
  Multiplexer #(.enable("false")) multiplexer_84 (
    .in0(multiplexer_52_out), .in1(multiplexer_56_out), .out(multiplexer_84_out), .sel(move[2]));
  Multiplexer #(.enable("false")) multiplexer_85 (
    .in0(multiplexer_53_out), .in1(multiplexer_57_out), .out(multiplexer_85_out), .sel(move[2]));
  Multiplexer #(.enable("false")) multiplexer_86 (
    .in0(multiplexer_54_out), .in1(multiplexer_58_out), .out(multiplexer_86_out), .sel(move[2]));
  Multiplexer #(.enable("false")) multiplexer_87 (
    .in0(multiplexer_55_out), .in1(multiplexer_59_out), .out(multiplexer_87_out), .sel(move[2]));
  Multiplexer #(.enable("false")) multiplexer_88 (
    .in0(multiplexer_56_out), .in1(multiplexer_60_out), .out(multiplexer_88_out), .sel(move[2]));
  Multiplexer #(.enable("false")) multiplexer_89 (
    .in0(multiplexer_57_out), .in1(multiplexer_61_out), .out(multiplexer_89_out), .sel(move[2]));
  Multiplexer #(.enable("false")) multiplexer_90 (
    .in0(multiplexer_58_out), .in1(multiplexer_62_out), .out(multiplexer_90_out), .sel(move[2]));
  Multiplexer #(.enable("false")) multiplexer_91 (
    .in0(multiplexer_59_out), .in1(multiplexer_63_out), .out(multiplexer_91_out), .sel(move[2]));
  Multiplexer #(.enable("false")) multiplexer_92 (
    .in0(multiplexer_60_out), .in1(multiplexer_64_out), .out(multiplexer_92_out), .sel(move[2]));
  Multiplexer #(.enable("false")) multiplexer_93 (
    .in0(multiplexer_61_out), .in1(multiplexer_33_out), .out(multiplexer_93_out), .sel(move[2]));
  Multiplexer #(.enable("false")) multiplexer_94 (
    .in0(multiplexer_62_out), .in1(multiplexer_34_out), .out(multiplexer_94_out), .sel(move[2]));
  Multiplexer #(.enable("false")) multiplexer_95 (
    .in0(multiplexer_63_out), .in1(multiplexer_35_out), .out(multiplexer_95_out), .sel(move[2]));
  Multiplexer #(.enable("false")) multiplexer_96 (
    .in0(multiplexer_64_out), .in1(multiplexer_36_out), .out(multiplexer_96_out), .sel(move[2]));
  or or_1 (or_1_out[0], and_2_out, and_3_out, and_4_out, and_5_out);
  Multiplexer #(.enable("false")) multiplexer_97 (
    .in0(multiplexer_65_out), .in1(multiplexer_73_out), .out(multiplexer_97_out), .sel(move[3]));
  Multiplexer #(.enable("false")) multiplexer_98 (
    .in0(multiplexer_66_out), .in1(multiplexer_74_out), .out(multiplexer_98_out), .sel(move[3]));
  Multiplexer #(.enable("false")) multiplexer_99 (
    .in0(multiplexer_67_out), .in1(multiplexer_75_out), .out(multiplexer_99_out), .sel(move[3]));
  Multiplexer #(.enable("false")) multiplexer_100 (
    .in0(multiplexer_68_out), .in1(multiplexer_76_out), .out(multiplexer_100_out), .sel(move[3]));
  Multiplexer #(.enable("false")) multiplexer_101 (
    .in0(multiplexer_69_out), .in1(multiplexer_77_out), .out(multiplexer_101_out), .sel(move[3]));
  Multiplexer #(.enable("false")) multiplexer_102 (
    .in0(multiplexer_70_out), .in1(multiplexer_78_out), .out(multiplexer_102_out), .sel(move[3]));
  Multiplexer #(.enable("false")) multiplexer_103 (
    .in0(multiplexer_71_out), .in1(multiplexer_79_out), .out(multiplexer_103_out), .sel(move[3]));
  Multiplexer #(.enable("false")) multiplexer_104 (
    .in0(multiplexer_72_out), .in1(multiplexer_80_out), .out(multiplexer_104_out), .sel(move[3]));
  Multiplexer #(.enable("false")) multiplexer_105 (
    .in0(multiplexer_73_out), .in1(multiplexer_81_out), .out(multiplexer_105_out), .sel(move[3]));
  Multiplexer #(.enable("false")) multiplexer_106 (
    .in0(multiplexer_74_out), .in1(multiplexer_82_out), .out(multiplexer_106_out), .sel(move[3]));
  Multiplexer #(.enable("false")) multiplexer_107 (
    .in0(multiplexer_75_out), .in1(multiplexer_83_out), .out(multiplexer_107_out), .sel(move[3]));
  Multiplexer #(.enable("false")) multiplexer_108 (
    .in0(multiplexer_76_out), .in1(multiplexer_84_out), .out(multiplexer_108_out), .sel(move[3]));
  Multiplexer #(.enable("false")) multiplexer_109 (
    .in0(multiplexer_77_out), .in1(multiplexer_85_out), .out(multiplexer_109_out), .sel(move[3]));
  Multiplexer #(.enable("false")) multiplexer_110 (
    .in0(multiplexer_78_out), .in1(multiplexer_86_out), .out(multiplexer_110_out), .sel(move[3]));
  Multiplexer #(.enable("false")) multiplexer_111 (
    .in0(multiplexer_79_out), .in1(multiplexer_87_out), .out(multiplexer_111_out), .sel(move[3]));
  Multiplexer #(.enable("false")) multiplexer_112 (
    .in0(multiplexer_80_out), .in1(multiplexer_88_out), .out(multiplexer_112_out), .sel(move[3]));
  Multiplexer #(.enable("false")) multiplexer_113 (
    .in0(multiplexer_81_out), .in1(multiplexer_89_out), .out(multiplexer_113_out), .sel(move[3]));
  Multiplexer #(.enable("false")) multiplexer_114 (
    .in0(multiplexer_82_out), .in1(multiplexer_90_out), .out(multiplexer_114_out), .sel(move[3]));
  Multiplexer #(.enable("false")) multiplexer_115 (
    .in0(multiplexer_83_out), .in1(multiplexer_91_out), .out(multiplexer_115_out), .sel(move[3]));
  Multiplexer #(.enable("false")) multiplexer_116 (
    .in0(multiplexer_84_out), .in1(multiplexer_92_out), .out(multiplexer_116_out), .sel(move[3]));
  Multiplexer #(.enable("false")) multiplexer_117 (
    .in0(multiplexer_85_out), .in1(multiplexer_93_out), .out(multiplexer_117_out), .sel(move[3]));
  Multiplexer #(.enable("false")) multiplexer_118 (
    .in0(multiplexer_86_out), .in1(multiplexer_94_out), .out(multiplexer_118_out), .sel(move[3]));
  Multiplexer #(.enable("false")) multiplexer_119 (
    .in0(multiplexer_87_out), .in1(multiplexer_95_out), .out(multiplexer_119_out), .sel(move[3]));
  Multiplexer #(.enable("false")) multiplexer_120 (
    .in0(multiplexer_88_out), .in1(multiplexer_96_out), .out(multiplexer_120_out), .sel(move[3]));
  Multiplexer #(.enable("false")) multiplexer_121 (
    .in0(multiplexer_89_out), .in1(multiplexer_65_out), .out(multiplexer_121_out), .sel(move[3]));
  Multiplexer #(.enable("false")) multiplexer_122 (
    .in0(multiplexer_90_out), .in1(multiplexer_66_out), .out(multiplexer_122_out), .sel(move[3]));
  Multiplexer #(.enable("false")) multiplexer_123 (
    .in0(multiplexer_91_out), .in1(multiplexer_67_out), .out(multiplexer_123_out), .sel(move[3]));
  Multiplexer #(.enable("false")) multiplexer_124 (
    .in0(multiplexer_92_out), .in1(multiplexer_68_out), .out(multiplexer_124_out), .sel(move[3]));
  Multiplexer #(.enable("false")) multiplexer_125 (
    .in0(multiplexer_93_out), .in1(multiplexer_69_out), .out(multiplexer_125_out), .sel(move[3]));
  Multiplexer #(.enable("false")) multiplexer_126 (
    .in0(multiplexer_94_out), .in1(multiplexer_70_out), .out(multiplexer_126_out), .sel(move[3]));
  Multiplexer #(.enable("false")) multiplexer_127 (
    .in0(multiplexer_95_out), .in1(multiplexer_71_out), .out(multiplexer_127_out), .sel(move[3]));
  Multiplexer #(.enable("false")) multiplexer_128 (
    .in0(multiplexer_96_out), .in1(multiplexer_72_out), .out(multiplexer_128_out), .sel(move[3]));
  Multiplexer #(.enable("false")) multiplexer_129 (
    .in0(multiplexer_97_out), .in1(multiplexer_113_out), .out(multiplexer_129_out), .sel(move[4]));
  Multiplexer #(.enable("false")) multiplexer_130 (
    .in0(multiplexer_98_out), .in1(multiplexer_114_out), .out(multiplexer_130_out), .sel(move[4]));
  Multiplexer #(.enable("false")) multiplexer_131 (
    .in0(multiplexer_99_out), .in1(multiplexer_115_out), .out(multiplexer_131_out), .sel(move[4]));
  Multiplexer #(.enable("false")) multiplexer_132 (
    .in0(multiplexer_100_out), .in1(multiplexer_116_out), .out(multiplexer_132_out), .sel(move[4]));
  Multiplexer #(.enable("false")) multiplexer_133 (
    .in0(multiplexer_101_out), .in1(multiplexer_117_out), .out(multiplexer_133_out), .sel(move[4]));
  Multiplexer #(.enable("false")) multiplexer_134 (
    .in0(multiplexer_102_out), .in1(multiplexer_118_out), .out(multiplexer_134_out), .sel(move[4]));
  Multiplexer #(.enable("false")) multiplexer_135 (
    .in0(multiplexer_103_out), .in1(multiplexer_119_out), .out(multiplexer_135_out), .sel(move[4]));
  Multiplexer #(.enable("false")) multiplexer_136 (
    .in0(multiplexer_104_out), .in1(multiplexer_120_out), .out(multiplexer_136_out), .sel(move[4]));
  Multiplexer #(.enable("false")) multiplexer_137 (
    .in0(multiplexer_105_out), .in1(multiplexer_121_out), .out(multiplexer_137_out), .sel(move[4]));
  Multiplexer #(.enable("false")) multiplexer_138 (
    .in0(multiplexer_106_out), .in1(multiplexer_122_out), .out(multiplexer_138_out), .sel(move[4]));
  Multiplexer #(.enable("false")) multiplexer_139 (
    .in0(multiplexer_107_out), .in1(multiplexer_123_out), .out(multiplexer_139_out), .sel(move[4]));
  Multiplexer #(.enable("false")) multiplexer_140 (
    .in0(multiplexer_108_out), .in1(multiplexer_124_out), .out(multiplexer_140_out), .sel(move[4]));
  Multiplexer #(.enable("false")) multiplexer_141 (
    .in0(multiplexer_109_out), .in1(multiplexer_125_out), .out(multiplexer_141_out), .sel(move[4]));
  Multiplexer #(.enable("false")) multiplexer_142 (
    .in0(multiplexer_110_out), .in1(multiplexer_126_out), .out(multiplexer_142_out), .sel(move[4]));
  Multiplexer #(.enable("false")) multiplexer_143 (
    .in0(multiplexer_111_out), .in1(multiplexer_127_out), .out(multiplexer_143_out), .sel(move[4]));
  Multiplexer #(.enable("false")) multiplexer_144 (
    .in0(multiplexer_112_out), .in1(multiplexer_128_out), .out(multiplexer_144_out), .sel(move[4]));
  Multiplexer #(.enable("false")) multiplexer_145 (
    .in0(multiplexer_113_out), .in1(multiplexer_97_out), .out(multiplexer_145_out), .sel(move[4]));
  Multiplexer #(.enable("false")) multiplexer_146 (
    .in0(multiplexer_114_out), .in1(multiplexer_98_out), .out(multiplexer_146_out), .sel(move[4]));
  Multiplexer #(.enable("false")) multiplexer_147 (
    .in0(multiplexer_115_out), .in1(multiplexer_99_out), .out(multiplexer_147_out), .sel(move[4]));
  Multiplexer #(.enable("false")) multiplexer_148 (
    .in0(multiplexer_116_out), .in1(multiplexer_100_out), .out(multiplexer_148_out), .sel(move[4]));
  Multiplexer #(.enable("false")) multiplexer_149 (
    .in0(multiplexer_117_out), .in1(multiplexer_101_out), .out(multiplexer_149_out), .sel(move[4]));
  Multiplexer #(.enable("false")) multiplexer_150 (
    .in0(multiplexer_118_out), .in1(multiplexer_102_out), .out(multiplexer_150_out), .sel(move[4]));
  Multiplexer #(.enable("false")) multiplexer_151 (
    .in0(multiplexer_119_out), .in1(multiplexer_103_out), .out(multiplexer_151_out), .sel(move[4]));
  Multiplexer #(.enable("false")) multiplexer_152 (
    .in0(multiplexer_120_out), .in1(multiplexer_104_out), .out(multiplexer_152_out), .sel(move[4]));
  Multiplexer #(.enable("false")) multiplexer_153 (
    .in0(multiplexer_121_out), .in1(multiplexer_105_out), .out(multiplexer_153_out), .sel(move[4]));
  Multiplexer #(.enable("false")) multiplexer_154 (
    .in0(multiplexer_122_out), .in1(multiplexer_106_out), .out(multiplexer_154_out), .sel(move[4]));
  Multiplexer #(.enable("false")) multiplexer_155 (
    .in0(multiplexer_123_out), .in1(multiplexer_107_out), .out(multiplexer_155_out), .sel(move[4]));
  Multiplexer #(.enable("false")) multiplexer_156 (
    .in0(multiplexer_124_out), .in1(multiplexer_108_out), .out(multiplexer_156_out), .sel(move[4]));
  Multiplexer #(.enable("false")) multiplexer_157 (
    .in0(multiplexer_125_out), .in1(multiplexer_109_out), .out(multiplexer_157_out), .sel(move[4]));
  Multiplexer #(.enable("false")) multiplexer_158 (
    .in0(multiplexer_126_out), .in1(multiplexer_110_out), .out(multiplexer_158_out), .sel(move[4]));
  Multiplexer #(.enable("false")) multiplexer_159 (
    .in0(multiplexer_127_out), .in1(multiplexer_111_out), .out(multiplexer_159_out), .sel(move[4]));
  Multiplexer #(.enable("false")) multiplexer_160 (
    .in0(multiplexer_128_out), .in1(multiplexer_112_out), .out(multiplexer_160_out), .sel(move[4]));
  Multiplexer #(.select(2), .enable("false")) multiplexer_161 (
    .in0(multiplexer_160_out), .in1(in_1[31]), .out(out_4[31]), .sel(or_1_out));  // open: in2, in3
  Multiplexer #(.select(2), .enable("false")) multiplexer_162 (
    .in0(multiplexer_159_out), .in1(in_1[30]), .out(out_4[30]), .sel(or_1_out));  // open: in2, in3
  Multiplexer #(.select(2), .enable("false")) multiplexer_163 (
    .in0(multiplexer_158_out), .in1(in_1[29]), .out(out_4[29]), .sel(or_1_out));  // open: in2, in3
  Multiplexer #(.select(2), .enable("false")) multiplexer_164 (
    .in0(multiplexer_157_out), .in1(in_1[28]), .out(out_4[28]), .sel(or_1_out));  // open: in2, in3
  Multiplexer #(.select(2), .enable("false")) multiplexer_165 (
    .in0(multiplexer_156_out), .in1(in_1[27]), .out(out_4[27]), .sel(or_1_out));  // open: in2, in3
  Multiplexer #(.select(2), .enable("false")) multiplexer_166 (
    .in0(multiplexer_155_out), .in1(in_1[26]), .out(out_4[26]), .sel(or_1_out));  // open: in2, in3
  Multiplexer #(.select(2), .enable("false")) multiplexer_167 (
    .in0(multiplexer_154_out), .in1(in_1[25]), .out(out_4[25]), .sel(or_1_out));  // open: in2, in3
  Multiplexer #(.select(2), .enable("false")) multiplexer_168 (
    .in0(multiplexer_153_out), .in1(in_1[24]), .out(out_4[24]), .sel(or_1_out));  // open: in2, in3
  Multiplexer #(.select(2), .enable("false")) multiplexer_169 (
    .in0(multiplexer_152_out), .in1(in_1[23]), .out(out_4[23]), .sel(or_1_out));  // open: in2, in3
  Multiplexer #(.select(2), .enable("false")) multiplexer_170 (
    .in0(multiplexer_151_out), .in1(in_1[22]), .out(out_4[22]), .sel(or_1_out));  // open: in2, in3
  Multiplexer #(.select(2), .enable("false")) multiplexer_171 (
    .in0(multiplexer_150_out), .in1(in_1[21]), .out(out_4[21]), .sel(or_1_out));  // open: in2, in3
  Multiplexer #(.select(2), .enable("false")) multiplexer_172 (
    .in0(multiplexer_149_out), .in1(in_1[20]), .out(out_4[20]), .sel(or_1_out));  // open: in2, in3
  Multiplexer #(.select(2), .enable("false")) multiplexer_173 (
    .in0(multiplexer_148_out), .in1(in_1[19]), .out(out_4[19]), .sel(or_1_out));  // open: in2, in3
  Multiplexer #(.select(2), .enable("false")) multiplexer_174 (
    .in0(multiplexer_147_out), .in1(in_1[18]), .out(out_4[18]), .sel(or_1_out));  // open: in2, in3
  Multiplexer #(.select(2), .enable("false")) multiplexer_175 (
    .in0(multiplexer_146_out), .in1(in_1[17]), .out(out_4[17]), .sel(or_1_out));  // open: in2, in3
  Multiplexer #(.select(2), .enable("false")) multiplexer_176 (
    .in0(multiplexer_145_out), .in1(in_1[16]), .out(out_4[16]), .sel(or_1_out));  // open: in2, in3
  Multiplexer #(.select(2), .enable("false")) multiplexer_177 (
    .in0(multiplexer_144_out), .in1(in_1[15]), .out(out_4[15]), .sel(or_1_out));  // open: in2, in3
  Multiplexer #(.select(2), .enable("false")) multiplexer_178 (
    .in0(multiplexer_143_out), .in1(in_1[14]), .out(out_4[14]), .sel(or_1_out));  // open: in2, in3
  Multiplexer #(.select(2), .enable("false")) multiplexer_179 (
    .in0(multiplexer_142_out), .in1(in_1[13]), .out(out_4[13]), .sel(or_1_out));  // open: in2, in3
  Multiplexer #(.select(2), .enable("false")) multiplexer_180 (
    .in0(multiplexer_141_out), .in1(in_1[12]), .out(out_4[12]), .sel(or_1_out));  // open: in2, in3
  Multiplexer #(.select(2), .enable("false")) multiplexer_181 (
    .in0(multiplexer_140_out), .in1(in_1[11]), .out(out_4[11]), .sel(or_1_out));  // open: in2, in3
  Multiplexer #(.select(2), .enable("false")) multiplexer_182 (
    .in0(multiplexer_139_out), .in1(in_1[10]), .out(out_4[10]), .sel(or_1_out));  // open: in2, in3
  Multiplexer #(.select(2), .enable("false")) multiplexer_183 (
    .in0(multiplexer_138_out), .in1(in_1[9]), .out(out_4[9]), .sel(or_1_out));  // open: in2, in3
  Multiplexer #(.select(2), .enable("false")) multiplexer_184 (
    .in0(multiplexer_137_out), .in1(in_1[8]), .out(out_4[8]), .sel(or_1_out));  // open: in2, in3
  Multiplexer #(.select(2), .enable("false")) multiplexer_185 (
    .in0(multiplexer_136_out), .in1(in_1[7]), .out(out_4[7]), .sel(or_1_out));  // open: in2, in3
  Multiplexer #(.select(2), .enable("false")) multiplexer_186 (
    .in0(multiplexer_135_out), .in1(in_1[6]), .out(out_4[6]), .sel(or_1_out));  // open: in2, in3
  Multiplexer #(.select(2), .enable("false")) multiplexer_187 (
    .in0(multiplexer_134_out), .in1(in_1[5]), .out(out_4[5]), .sel(or_1_out));  // open: in2, in3
  Multiplexer #(.select(2), .enable("false")) multiplexer_188 (
    .in0(multiplexer_133_out), .in1(in_1[4]), .out(out_4[4]), .sel(or_1_out));  // open: in2, in3
  Multiplexer #(.select(2), .enable("false")) multiplexer_189 (
    .in0(multiplexer_132_out), .in1(in_1[3]), .out(out_4[3]), .sel(or_1_out));  // open: in2, in3
  Multiplexer #(.select(2), .enable("false")) multiplexer_190 (
    .in0(multiplexer_131_out), .in1(in_1[2]), .out(out_4[2]), .sel(or_1_out));  // open: in2, in3
  Multiplexer #(.select(2), .enable("false")) multiplexer_191 (
    .in0(multiplexer_130_out), .in1(in_1[1]), .out(out_4[1]), .sel(or_1_out));  // open: in2, in3
  Multiplexer #(.select(2), .enable("false")) multiplexer_192 (
    .in0(multiplexer_129_out), .in1(in_1[0]), .out(out_4[0]), .sel(or_1_out));  // open: in2, in3
endmodule

module teste (
  input  a,
  input  b,
  input  c,
  input  d,
  input  e,
  output s1,
  output s0
);

  wire and_2_out, and_3_out, and_4_out, and_5_out, not_1_out, not_2_out, not_3_out, not_4_out, not_5_out,
       not_6_out, not_7_out, not_8_out, not_9_out, not_10_out, not_11_out, not_12_out, not_13_out,
       not_14_out, not_15_out;

  not not_1 (not_1_out, a);
  not not_2 (not_2_out, c);
  not not_3 (not_3_out, d);
  not not_4 (not_4_out, a);
  not not_5 (not_5_out, b);
  not not_6 (not_6_out, c);
  not not_7 (not_7_out, a);
  not not_8 (not_8_out, b);
  not not_9 (not_9_out, d);
  not not_10 (not_10_out, a);
  not not_11 (not_11_out, b);
  not not_12 (not_12_out, e);
  not not_13 (not_13_out, a);
  not not_14 (not_14_out, c);
  not not_15 (not_15_out, d);
  and and_1 (s1, not_1_out, b, not_2_out, not_3_out);
  and and_2 (and_2_out, not_4_out, not_5_out, not_6_out);
  and and_3 (and_3_out, not_7_out, not_8_out, not_9_out);
  and and_4 (and_4_out, not_10_out, not_11_out, not_12_out);
  and and_5 (and_5_out, not_13_out, not_14_out, not_15_out, e);
  or or_1 (s0, and_2_out, and_3_out, and_4_out, and_5_out);
endmodule
